// Logisim project BreadboardComputer.circ as structural Verilog: 1 circuit, main circuit main
module main (
);

  S_R_Flip_Flop s_r_ff_1 ();  // open: S, R, clk, Q, reset, Qn, preset
  D_Flip_Flop d_ff_1 ();  // open: D, clk, Q, Qn, preset, reset
  // Shift_Register shift_register_1: pin names not known
endmodule
